// Logisim project CPU_LAB4.circ as structural Verilog: 4 circuits, main circuit main
module main (
  input  [15:0] Instruction,
  input  Clk,
  input  in_3,
  output [4:0] Instruction_Address_Out,
  output [3:0] Reg0_Out,
  output [3:0] Reg1_Out,
  output [3:0] Reg2_Out,
  output [3:0] Reg3_Out,
  output [3:0] Reg4_Out,
  output [3:0] Reg5_Out,
  output [3:0] Reg6_Out,
  output [3:0] Reg7_Out,
  output [3:0] Reg8_Out,
  output [3:0] Reg9_Out,
  output [3:0] Reg10_Out,
  output [3:0] Reg11_Out,
  output [3:0] Reg12_Out,
  output [3:0] Reg13_Out,
  output [3:0] Reg14_Out,
  output [3:0] Reg15_Out
);

  wire [3:0] A_Value, B_Value;

  registers registers_1 (
    .A_Out(A_Value), .B_Out(B_Value), .Reg0_Out(Reg0_Out), .Reg1_Out(Reg1_Out), .Reg2_Out(Reg2_Out),
    .Reg3_Out(Reg3_Out), .Reg4_Out(Reg4_Out), .Reg5_Out(Reg5_Out), .Reg6_Out(Reg6_Out), .Reg7_Out(Reg7_Out),
    .Reg8_Out(Reg8_Out), .Reg9_Out(Reg9_Out), .Reg10_Out(Reg10_Out), .Reg11_Out(Reg11_Out),
    .Reg12_Out(Reg12_Out), .Reg13_Out(Reg13_Out), .Reg14_Out(Reg14_Out), .Reg15_Out(Reg15_Out));  // open: A_Sel_In, B_Sel_In, C_Sel_In, Data_In, Reg_Write_In, clk_in

  // Other names for the same wires on the sheet: ClkIn = Clk; Instruction_Address[4:0] = Instruction_Address_Out;
  //   Reg0[3:0] = Reg0_Out; Reg1[3:0] = Reg1_Out; Reg2[3:0] = Reg2_Out; Reg3[3:0] = Reg3_Out; Reg4[3:0] = Reg4_Out;
  //   Reg5[3:0] = Reg5_Out; Reg6[3:0] = Reg6_Out; Reg7[3:0] = Reg7_Out; Reg8[3:0] = Reg8_Out; Reg9[3:0] = Reg9_Out;
  //   Reg10[3:0] = Reg10_Out; Reg11[3:0] = Reg11_Out; Reg12[3:0] = Reg12_Out; Reg13[3:0] = Reg13_Out;
  //   Reg14[3:0] = Reg14_Out; Reg15[3:0] = Reg15_Out
endmodule

module registers (
  input  [3:0] A_Sel_In,
  input  [3:0] B_Sel_In,
  input  [3:0] C_Sel_In,
  input  [3:0] Data_In,
  input  Reg_Write_In,
  input  clk_in,
  output [3:0] A_Out,
  output [3:0] B_Out,
  output [3:0] Reg0_Out,
  output [3:0] Reg1_Out,
  output [3:0] Reg2_Out,
  output [3:0] Reg3_Out,
  output [3:0] Reg4_Out,
  output [3:0] Reg5_Out,
  output [3:0] Reg6_Out,
  output [3:0] Reg7_Out,
  output [3:0] Reg8_Out,
  output [3:0] Reg9_Out,
  output [3:0] Reg10_Out,
  output [3:0] Reg11_Out,
  output [3:0] Reg12_Out,
  output [3:0] Reg13_Out,
  output [3:0] Reg14_Out,
  output [3:0] Reg15_Out
);

  wire Reg_Write0, Reg_Write1, Reg_Write2, Reg_Write3, Reg_Write4, Reg_Write5, Reg_Write6, Reg_Write7,
       Reg_Write8, Reg_Write9, Reg_Write10, Reg_Write11, Reg_Write12, Reg_Write13, Reg_Write14, Reg_Write15;

  Demultiplexer #(.select(4), .enable("false")) demultiplexer_1 (
    .out0(Reg_Write0), .out1(Reg_Write1), .out2(Reg_Write2), .out3(Reg_Write3), .out4(Reg_Write4),
    .out5(Reg_Write5), .out6(Reg_Write6), .out7(Reg_Write7), .out8(Reg_Write8), .out9(Reg_Write9),
    .out10(Reg_Write10), .out11(Reg_Write11), .out12(Reg_Write12), .out13(Reg_Write13), .out14(Reg_Write14),
    .out15(Reg_Write15), .in(Reg_Write_In), .sel(C_Sel_In));
  Multiplexer #(.select(4), .width(4), .enable("false")) multiplexer_1 (
    .in0(Reg0_Out), .in1(Reg1_Out), .in2(Reg2_Out), .in3(Reg3_Out), .in4(Reg4_Out), .in5(Reg5_Out),
    .in6(Reg6_Out), .in7(Reg7_Out), .in8(Reg8_Out), .in9(Reg9_Out), .in10(Reg10_Out), .in11(Reg11_Out),
    .in12(Reg12_Out), .in13(Reg13_Out), .in14(Reg14_Out), .in15(Reg15_Out), .out(A_Out), .sel(A_Sel_In));
  Register #(.width(4)) register_1 (.D(Data_In), .en(Reg_Write0), .Q(Reg0_Out), .clk(clk_in));  // open: clr
  Register #(.width(4)) register_2 (.D(Data_In), .en(Reg_Write1), .Q(Reg1_Out), .clk(clk_in));  // open: clr
  Register #(.width(4)) register_3 (.D(Data_In), .en(Reg_Write2), .Q(Reg2_Out), .clk(clk_in));  // open: clr
  Register #(.width(4)) register_4 (.D(Data_In), .en(Reg_Write3), .Q(Reg3_Out), .clk(clk_in));  // open: clr
  Register #(.width(4)) register_5 (.D(Data_In), .en(Reg_Write4), .Q(Reg4_Out), .clk(clk_in));  // open: clr
  Register #(.width(4)) register_6 (.D(Data_In), .en(Reg_Write5), .Q(Reg5_Out), .clk(clk_in));  // open: clr
  Register #(.width(4)) register_7 (.D(Data_In), .en(Reg_Write6), .Q(Reg6_Out), .clk(clk_in));  // open: clr
  Register #(.width(4)) register_8 (.D(Data_In), .en(Reg_Write7), .Q(Reg7_Out), .clk(clk_in));  // open: clr
  Multiplexer #(.select(4), .width(4), .enable("false")) multiplexer_2 (
    .in0(Reg0_Out), .in1(Reg1_Out), .in2(Reg2_Out), .in3(Reg3_Out), .in4(Reg4_Out), .in5(Reg5_Out),
    .in6(Reg6_Out), .in7(Reg7_Out), .in8(Reg8_Out), .in9(Reg9_Out), .in10(Reg10_Out), .in11(Reg11_Out),
    .in12(Reg12_Out), .in13(Reg13_Out), .in14(Reg14_Out), .in15(Reg15_Out), .out(B_Out), .sel(B_Sel_In));
  Register #(.width(4)) register_9 (.D(Data_In), .en(Reg_Write8), .Q(Reg8_Out), .clk(clk_in));  // open: clr
  Register #(.width(4)) register_10 (.D(Data_In), .en(Reg_Write9), .Q(Reg9_Out), .clk(clk_in));  // open: clr
  Register #(.width(4)) register_11 (.D(Data_In), .en(Reg_Write10), .Q(Reg10_Out), .clk(clk_in));  // open: clr
  Register #(.width(4)) register_12 (.D(Data_In), .en(Reg_Write11), .Q(Reg11_Out), .clk(clk_in));  // open: clr
  Register #(.width(4)) register_13 (.D(Data_In), .en(Reg_Write12), .Q(Reg12_Out), .clk(clk_in));  // open: clr
  Register #(.width(4)) register_14 (.D(Data_In), .en(Reg_Write13), .Q(Reg13_Out), .clk(clk_in));  // open: clr
  Register #(.width(4)) register_15 (.D(Data_In), .en(Reg_Write14), .Q(Reg14_Out), .clk(clk_in));  // open: clr
  Register #(.width(4)) register_16 (.D(Data_In), .en(Reg_Write15), .Q(Reg15_Out), .clk(clk_in));  // open: clr

  // Other names for the same wires on the sheet: A[3:0] = A_Out; A_Sel[3:0] = A_Sel_In; B[3:0] = B_Out;
  //   B_Sel[3:0] = B_Sel_In; C_Sel[3:0] = C_Sel_In; clk = clk_in; Data[3:0] = Data_In; Reg0[3:0] = Reg0_Out;
  //   Reg1[3:0] = Reg1_Out; Reg2[3:0] = Reg2_Out; Reg3[3:0] = Reg3_Out; Reg4[3:0] = Reg4_Out; Reg5[3:0] = Reg5_Out;
  //   Reg6[3:0] = Reg6_Out; Reg7[3:0] = Reg7_Out; Reg8[3:0] = Reg8_Out; Reg9[3:0] = Reg9_Out; Reg10[3:0] = Reg10_Out;
  //   Reg11[3:0] = Reg11_Out; Reg12[3:0] = Reg12_Out; Reg13[3:0] = Reg13_Out; Reg14[3:0] = Reg14_Out;
  //   Reg15[3:0] = Reg15_Out; Reg_Write = Reg_Write_In
endmodule

module CPU (
);

  Register #(.width(16)) register_1 ();  // open: D, en, Q, clk, clr
  registers registers ();  // open: A_Sel_In, B_Sel_In, C_Sel_In, Data_In, Reg_Write_In, clk_in, A_Out, B_Out, Reg0_Out, Reg1_Out, Reg2_Out, Reg3_Out, Reg4_Out, Reg5_Out, Reg6_Out, Reg7_Out, Reg8_Out, Reg9_Out, Reg10_Out, Reg11_Out, Reg12_Out, Reg13_Out, Reg14_Out, Reg15_Out
endmodule

module ALU (
  input  [3:0] A_Sel_in,
  input  [3:0] B_Sel_in,
  input  [3:0] OpCode,
  output [3:0] C_Sel_out
);

  wire [3:0] ADDR, ANDR, Negate, NOT, ORR, SUBR, XORR;

  assign NOT = ~A_Sel_in;  // NOT_Gate not_1, 4 bits wide
  assign ANDR = A_Sel_in & B_Sel_in;  // AND_Gate and_1, 4 bits wide
  assign ORR = A_Sel_in | B_Sel_in;  // OR_Gate or_1, 4 bits wide
  assign XORR = A_Sel_in ^ B_Sel_in;  // XOR_Gate xor_1, 4 bits wide
  Adder #(.width(4)) adder_1 (.a(A_Sel_in), .b(B_Sel_in), .out(ADDR));  // open: cin, cout
  Subtractor #(.width(4)) subtractor_1 (.a(A_Sel_in), .b(B_Sel_in), .out(SUBR));  // open: bin, bout
  Negator #(.width(4)) negator_1 (.in(A_Sel_in), .out(Negate));
  Multiplexer #(.select(4), .width(4), .enable("false")) multiplexer_1 (
    .in2(B_Sel_in), .in3(A_Sel_in), .in4(ANDR), .in5(ORR), .in6(XORR), .in7(NOT), .in8(ADDR), .in9(SUBR),
    .in10(Negate), .in11(A_Sel_in), .out(C_Sel_out), .sel(OpCode));  // open: in0, in1, in12, in13, in14, in15

  // Other names for the same wires on the sheet: B_Sel[3:0] = B_Sel_in; C_out[3:0] = C_Sel_out; A_Sel[3:0] = A_Sel_in;
  //   MOVE[3:0] = A_Sel_in; OP[3:0] = OpCode
endmodule
